// Logisim project lab7-1.circ as structural Verilog: 1 circuit, main circuit main
module main (
  input  Pc,
  input  Inc,
  input  Amux,
  input  Mar,
  input  Mst,
  input  Ir,
  input  Dmux,
  input  Acc,
  input  Out,
  input  Sub,
  output [7:0] out_11
);

  wire and_1_out, clock_1_out, Clr_out, Halt_out;
  wire [3:0] Ir_q, Mar_q, multiplexer_1_out, not_1_out, Pc_q;
  wire [7:0] Acc_q, adder_1_out, multiplexer_2_out, ram_1_data, xor_1_out;
  wire [7:4] Ir_q_2;

  Clock clock_1 (.out(clock_1_out));
  and and_1 (and_1_out, clock_1_out, Halt_out);
  Button Clr (.out(Clr_out));
  Multiplexer #(.width(4), .enable("false")) multiplexer_1 (
    .in0(Pc_q), .in1(Ir_q), .out(multiplexer_1_out), .sel(Amux));
  Counter #(.width(4), .max('hf)) u_Pc (
    .load(Pc), .D(Ir_q), .count(Inc), .Q(Pc_q), .clk(and_1_out), .clr(Clr_out));  // open: carry
  Register #(.width(4)) u_Mar (.D(multiplexer_1_out), .en(Mar), .Q(Mar_q), .clk(and_1_out));  // open: clr
  RAM #(.addrWidth(4), .bus("separate")) ram_1 (
    .addr(Mar_q), .din(Acc_q), .data(ram_1_data), .str(Mst), .clk(and_1_out));  // open: sel, ld, clr
  Multiplexer #(.width(8), .enable("false")) multiplexer_2 (
    .in0(adder_1_out), .in1(ram_1_data), .out(multiplexer_2_out), .sel(Dmux));
  Register u_Ir (.D(ram_1_data), .en(Ir), .Q({Ir_q_2, Ir_q}), .clk(and_1_out), .clr(Clr_out));
  Register u_Acc (.D(multiplexer_2_out), .en(Acc), .Q(Acc_q), .clk(and_1_out));  // open: clr
  Register u_Out (.D(Acc_q), .en(Out), .Q(out_11), .clk(and_1_out));  // open: clr
  assign xor_1_out = ram_1_data ^ {8{Sub}};  // XOR_Gate xor_1, 8 bits wide
  nand Halt (Halt_out, Ir_q_2[7], Ir_q_2[6], Ir_q_2[5], Ir_q_2[4]);
  Adder adder_1 (.a(Acc_q), .b(xor_1_out), .out(adder_1_out), .cin(Sub));  // open: cout
  assign not_1_out = ~Ir_q_2;  // NOT_Gate not_1, 4 bits wide
endmodule
